// Logisim project AlgorithmiqueDesCircuits.circ as structural Verilog: 8 circuits, main circuit main
module main (
  input  [6:0] \Entrée ,
  input  [6:0] \Entrée_2 ,
  input  [6:0] \Entrée_3 ,
  input  H,
  input  init,
  output [6:0] Sortie,
  output [6:0] Sortie_2,
  output fini,
  output [6:0] Sortie_3
);

  wire bouclefinie_1_s, choix_1_s;
  wire [6:0] alors_1_s, corpsdeboucle_1_s, multiplexer_1_out, premier_1_s, sinon_1_s;

  Multiplexer #(.width(7), .enable("false")) multiplexer_1 (
    .in0(corpsdeboucle_1_s), .in1(\Entrée_3 ), .out(multiplexer_1_out), .sel(init));
  Premier premier_1 (.E(\Entrée ), .S(premier_1_s));
  Choix choix_1 (.E(\Entrée_2 ), .S(choix_1_s));
  Sinon sinon_1 (.E(\Entrée_2 ), .S(sinon_1_s));
  Alors alors_1 (.E(\Entrée_2 ), .S(alors_1_s));
  Register #(.width(7)) \Mémoire  (.D(multiplexer_1_out), .en(bouclefinie_1_s), .Q(Sortie_3), .clk(H));  // open: clr
  Second second_1 (.E(premier_1_s), .S(Sortie));
  Multiplexer #(.width(7), .enable("false")) multiplexer_2 (
    .in0(sinon_1_s), .in1(alors_1_s), .out(Sortie_2), .sel(choix_1_s));
  CorpsDeBoucle corpsdeboucle_1 (.E(Sortie_3), .S(corpsdeboucle_1_s));
  BoucleFinie bouclefinie_1 (.E(Sortie_3), .S(bouclefinie_1_s));
  not not_1 (fini, bouclefinie_1_s);

  // Notes on the sheet:
  //   Algorithmique des circuits
  //   Séquence : Premier ; Second
  //   Boucle : Tant que (Continuer) faire CorpsDeBoucle 
  //   Conditionnelle : Si (Choix) faire Alors sinon faire Sinon
endmodule

module Premier (
  input  [6:0] E,
  output [6:0] S
);

  wire [2:0] bitadder_1_out;
  wire [6:0] shifter_1_out;

  BitAdder #(.width(7)) bitadder_1 (.in0(E), .out(bitadder_1_out));
  Shifter #(.width(7), .shift("rl")) shifter_1 (.in(E), .\dist (bitadder_1_out), .out(shifter_1_out));
  assign S = E & shifter_1_out;  // AND_Gate and_1, 7 bits wide
endmodule

module Second (
  input  [6:0] E,
  output [6:0] S
);

  wire [6:0] shifter_1_out;

  Shifter #(.width(7), .shift("rl")) shifter_1 (.in(E), .\dist (3'b001), .out(shifter_1_out));
  assign S = E | shifter_1_out;  // OR_Gate or_1, 7 bits wide
endmodule

module Choix (
  input  [6:0] E,
  output S
);

  wire [2:0] bitadder_1_out;

  BitAdder #(.width(7)) bitadder_1 (.in0(E), .out(bitadder_1_out));
  Comparator #(.width(3), .mode("unsigned")) comparator_1 (.a(bitadder_1_out), .b(3'b011), .gt(S));  // open: eq, lt
endmodule

// Continuer
module BoucleFinie (
  input  [6:0] E,
  output S
);

  wire comparator_1_eq, comparator_2_eq, or_1_out;
  wire [2:0] bitadder_1_out;

  BitAdder #(.width(7)) bitadder_1 (.in0(E), .out(bitadder_1_out));
  Comparator #(.width(3), .mode("unsigned")) comparator_1 (
    .a(bitadder_1_out), .b(3'b000), .eq(comparator_1_eq));  // open: gt, lt
  Comparator #(.width(3), .mode("unsigned")) comparator_2 (
    .a(bitadder_1_out), .b(3'b111), .eq(comparator_2_eq));  // open: gt, lt
  or or_1 (or_1_out, comparator_1_eq, comparator_2_eq);
  not not_1 (S, or_1_out);
endmodule

module Alors (
  input  [6:0] E,
  output [6:0] S
);

  wire [2:0] bitadder_1_out;
  wire [6:0] shifter_1_out;

  BitAdder #(.width(7)) bitadder_1 (.in0(E), .out(bitadder_1_out));
  Shifter #(.width(7), .shift("rl")) shifter_1 (.in(E), .\dist (bitadder_1_out), .out(shifter_1_out));
  assign S = E & shifter_1_out;  // AND_Gate and_1, 7 bits wide
endmodule

module Sinon (
  input  [6:0] E,
  output [6:0] S
);

  wire [6:0] shifter_1_out;

  Shifter #(.width(7), .shift("rl")) shifter_1 (.in(E), .\dist (3'b001), .out(shifter_1_out));
  assign S = E | shifter_1_out;  // OR_Gate or_1, 7 bits wide
endmodule

module CorpsDeBoucle (
  input  [6:0] E,
  output [6:0] S
);

  wire [2:0] bitadder_1_out;
  wire [6:0] shifter_1_out;

  BitAdder #(.width(7)) bitadder_1 (.in0(E), .out(bitadder_1_out));
  Shifter #(.width(7), .shift("rl")) shifter_1 (.in(E), .\dist (bitadder_1_out), .out(shifter_1_out));
  assign S = E & shifter_1_out;  // AND_Gate and_1, 7 bits wide
endmodule
