// Logisim project Euclide_PCPO.circ as structural Verilog: 2 circuits, main circuit main
module main (
  input  in_1,
  input  in_2,
  input  in_3,
  input  in_4,
  input  in_5,
  input  in_6,
  input  in_7,
  output out_8
);

  wire and_1_out, and_2_out, and_3_out, not_1_out, not_2_out, not_3_out, not_4_out, or_1_out, or_2_out,
       register_1_q, register_2_q;
  wire [6:0] subtractor_1_out;
  wire [7:0] A_q, B_q, multiplexer_1_out, multiplexer_2_out;

  not not_1 (not_1_out, in_1);
  Register #(.width(1)) register_1 (.D(or_2_out), .Q(register_1_q), .clk(in_3));  // open: en, clr
  not not_2 (not_2_out, in_2);
  not not_3 (not_3_out, register_1_q);
  Register A (.D({out_8, subtractor_1_out}), .Q(A_q), .clk(in_5));  // open: en, clr
  Register #(.width(1)) register_2 (.D(or_1_out), .Q(register_2_q), .clk(in_3));  // open: en, clr
  not not_4 (not_4_out, register_2_q);
  and and_1 (and_1_out, not_4_out, not_3_out, not_1_out);
  and and_2 (and_2_out, register_1_q, register_2_q);
  and and_3 (and_3_out, not_4_out, not_3_out, not_2_out);
  Register B (.D({out_8, subtractor_1_out}), .Q(B_q), .clk(in_6));  // open: en, clr
  or or_1 (or_1_out, and_1_out, and_2_out);
  or or_2 (or_2_out, and_2_out, and_3_out);
  Multiplexer #(.width(8), .enable("false")) multiplexer_1 (.in0(A_q), .in1(B_q), .out(multiplexer_1_out), .sel(in_4));
  Multiplexer #(.width(8), .enable("false")) multiplexer_2 (.in0(B_q), .in1(A_q), .out(multiplexer_2_out), .sel(in_7));
  Subtractor subtractor_1 (
    .a(multiplexer_1_out), .b(multiplexer_2_out), .out({out_8, subtractor_1_out}));  // open: bin, bout

  // Notes on the sheet:
  //   Entree Etat | Suiv
  //    !=   CMP | fin
  //   >  CMP | A
  //   <  CMP | B
  //   * CMP | fin
  //   *       A  | CMP
  //   *       B  | CMP
  //   *      fin  | fin
  //   Codage
  //   != : 00
  //   > : 01
  //   < : 10
  //   CMP : 00
  //   A : 01
  //   B : 10
  //   fin : 11
  //   PC (partie controle)
  //   PO (partie opérative)
endmodule

module pc_po (
  input  in_1
);

  wire and_1_out, and_2_out, and_3_out, not_1_out, not_2_out, not_3_out, or_1_out, or_2_out, register_1_q,
       register_2_q;
  wire [7:0] A_q, B_q, multiplexer_1_out, multiplexer_2_out, subtractor_1_out;

  Register #(.width(1)) register_1 (.D(or_2_out), .Q(register_1_q), .clk(in_1));  // open: en, clr
  not not_1 (not_1_out, subtractor_1_out[7]);
  Register #(.width(1)) register_2 (.D(or_1_out), .Q(register_2_q), .clk(in_1));  // open: en, clr
  not not_2 (not_2_out, register_1_q);
  not not_3 (not_3_out, register_2_q);
  Register A (.D(subtractor_1_out), .Q(A_q), .clk(register_2_q));  // open: en, clr
  and and_1 (and_1_out, not_3_out, not_2_out, not_1_out);
  and and_2 (and_2_out, register_1_q, register_2_q);
  and and_3 (and_3_out, not_3_out, not_2_out, subtractor_1_out[7]);
  Register #(.trigger("falling")) B (.D(subtractor_1_out), .Q(B_q), .clk(register_1_q));  // open: en, clr
  or or_1 (or_1_out, and_1_out, and_2_out);
  or or_2 (or_2_out, and_2_out, and_3_out);
  Multiplexer #(.width(8), .enable("false")) multiplexer_1 (
    .in0(A_q), .in1(B_q), .out(multiplexer_1_out), .sel(register_1_q));
  Subtractor subtractor_1 (.a(multiplexer_1_out), .b(multiplexer_2_out), .out(subtractor_1_out));  // open: bin, bout
  Multiplexer #(.width(8), .enable("false")) multiplexer_2 (
    .in0(A_q), .in1(B_q), .out(multiplexer_2_out), .sel(not_2_out));

  // Notes on the sheet:
  //   Essayer avec A = 12 (0C) et B = 8 ou 42 (2A) et 30 (1E) ou ... 
endmodule
