// Logisim project PO.circ as structural Verilog: 2 circuits, main circuit main
module main (
  input  [7:0] \Entrée ,
  input  D,
  input  Ecr,
  input  [1:0] Reg,
  input  [1:0] Op1,
  input  [1:0] Op0,
  input  [2:0] UAL,
  output [7:0] \Résultat ,
  output Z,
  output N
);

  wire decoder_1_out0, decoder_1_out1, decoder_1_out2, decoder_1_out3, Horloge_out;
  wire [7:0] multiplexer_1_out, multiplexer_2_out, multiplexer_3_out, R0_q, R1_q, R2_q, R3_q;

  Clock Horloge (.out(Horloge_out));
  Decoder #(.select(2), .disabled(0)) decoder_1 (
    .out0(decoder_1_out0), .out1(decoder_1_out1), .out2(decoder_1_out2), .out3(decoder_1_out3), .sel(Reg),
    .en(Ecr));
  Register R0 (.D(multiplexer_1_out), .en(decoder_1_out0), .Q(R0_q), .clk(Horloge_out));  // open: clr
  Multiplexer #(.width(8), .enable("false")) multiplexer_1 (
    .in0(\Entrée ), .in1(\Résultat ), .out(multiplexer_1_out), .sel(D));
  Register R1 (.D(multiplexer_1_out), .en(decoder_1_out1), .Q(R1_q), .clk(Horloge_out));  // open: clr
  Register R2 (.D(multiplexer_1_out), .en(decoder_1_out2), .Q(R2_q), .clk(Horloge_out));  // open: clr
  Register R3 (.D(multiplexer_1_out), .en(decoder_1_out3), .Q(R3_q), .clk(Horloge_out));  // open: clr
  Multiplexer #(.select(2), .width(8), .enable("false")) multiplexer_2 (
    .in0(R0_q), .in1(R1_q), .in2(R2_q), .in3(R3_q), .out(multiplexer_2_out), .sel(Op0));
  UAL ual_1 (.Op0(multiplexer_2_out), .Op1(multiplexer_3_out), .R(\Résultat ), .Fun(UAL), .N(N), .Z(Z));
  Multiplexer #(.select(2), .width(8), .enable("false")) multiplexer_3 (
    .in0(R0_q), .in1(R1_q), .in2(R2_q), .in3(R3_q), .out(multiplexer_3_out), .sel(Op1));

  // Notes on the sheet:
  //   0 : Op0
  //   Fun
  //   1 : /Op0 (inv)
  //   2 : Op0 >> 1
  //   3 : Op0 + Op1
  //   4 : Op0 - Op1
  //   5 : Op0 Et Op1
  //   6 : Op0 Ou Op1
  //   7 : Op0 OuEx Op1
endmodule

module UAL (
  input  [7:0] Op0,
  input  [7:0] Op1,
  input  [2:0] Fun,
  output [7:0] R,
  output N,
  output Z
);

  wire [7:0] adder_1_out, and_1_out, not_1_out, or_1_out, shifter_1_out, subtractor_1_out, xor_1_out;

  assign not_1_out = ~Op0;  // NOT_Gate not_1, 8 bits wide
  Shifter #(.shift("ar")) shifter_1 (.in(Op0), .\dist (3'b001), .out(shifter_1_out));
  Adder adder_1 (.a(Op0), .b(Op1), .out(adder_1_out), .cin(1'b0));  // open: cout
  Subtractor subtractor_1 (.a(Op0), .b(Op1), .out(subtractor_1_out), .bin(1'b0));  // open: bout
  assign and_1_out = Op0 & Op1;  // AND_Gate and_1, 8 bits wide
  assign or_1_out = Op0 | Op1;  // OR_Gate or_1, 8 bits wide
  assign xor_1_out = Op0 ^ Op1;  // XOR_Gate xor_1, 8 bits wide
  Multiplexer #(.select(3), .width(8), .enable("false")) multiplexer_1 (
    .in0(Op0), .in1(not_1_out), .in2(shifter_1_out), .in3(adder_1_out), .in4(subtractor_1_out),
    .in5(and_1_out), .in6(or_1_out), .in7(xor_1_out), .out({N, R[6:0]}), .sel(Fun));
  nor nor_1 (Z, N, R[6], R[5], R[4], R[3], R[2], R[1], R[0]);

  assign R[7] = N;
endmodule
