// Logisim project additionneur.circ as structural Verilog: 4 circuits, main circuit main
module main (
  input  in_1,
  input  A,
  input  B,
  input  A_2,
  input  B_2,
  input  A_3,
  input  B_3,
  input  A_4,
  input  B_4,
  output Res,
  output Res_2,
  output Res_3,
  output Res_4,
  output out_14
);

  wire and_1_out, and_2_out, and_3_out, and_4_out, and_5_out, and_6_out, and_7_out, and_8_out, or_1_out,
       or_2_out, or_3_out, xor_1_out, xor_2_out, xor_3_out, xor_4_out;

  xor xor_1 (xor_1_out, A, B);
  and and_1 (and_1_out, A, B);
  xor xor_2 (xor_2_out, A_2, B_2);
  and and_2 (and_2_out, A_2, B_2);
  xor xor_3 (xor_3_out, A_3, B_3);
  and and_3 (and_3_out, A_3, B_3);
  xor xor_4 (xor_4_out, A_4, B_4);
  and and_4 (and_4_out, A_4, B_4);
  or or_1 (or_1_out, and_1_out, and_5_out);
  or or_2 (or_2_out, and_2_out, and_6_out);
  or or_3 (or_3_out, and_3_out, and_7_out);
  or or_4 (out_14, and_4_out, and_8_out);
  xor xor_5 (Res, xor_1_out, in_1);
  and and_5 (and_5_out, xor_1_out, in_1);
  xor xor_6 (Res_2, xor_2_out, or_1_out);
  and and_6 (and_6_out, xor_2_out, or_1_out);
  xor xor_7 (Res_3, xor_3_out, or_2_out);
  and and_7 (and_7_out, xor_3_out, or_2_out);
  xor xor_8 (Res_4, xor_4_out, or_3_out);
  and and_8 (and_8_out, xor_4_out, or_3_out);

  // Notes on the sheet:
  //   1) Demi-additionneur
  //   2) Additionneur complet
  //   3) Additionneur 4 bits
  //   Création d'un additionneur
endmodule

module DemiAdd (
  input  A,
  input  B,
  output Res,
  output Ret
);

  xor xor_1 (Res, A, B);
  and and_1 (Ret, A, B);
endmodule

module Add (
  input  A,
  input  B,
  input  C,
  output Res,
  output Ret
);

  wire demiadd_1_res, demiadd_1_ret, demiadd_2_ret;

  DemiAdd demiadd_1 (.A(A), .B(B), .Res(demiadd_1_res), .Ret(demiadd_1_ret));
  DemiAdd demiadd_2 (.A(demiadd_1_res), .B(C), .Res(Res), .Ret(demiadd_2_ret));
  or or_1 (Ret, demiadd_2_ret, demiadd_1_ret);
endmodule

module Add4 (
  input  RetE,
  input  A0,
  input  B0,
  input  A1,
  input  B1,
  input  A2,
  input  B2,
  input  A3,
  input  B3,
  input  RetE_2,
  input  A0_2,
  input  A1_2,
  input  A2_2,
  input  A3_2,
  input  B0_2,
  input  B1_2,
  input  B2_2,
  input  B3_2,
  output Res0,
  output Res1,
  output Res2,
  output Res3,
  output RetS,
  output Res0_2,
  output Res1_2,
  output Res2_2,
  output Res3_2,
  output RetS_2
);

  wire add_1_ret, add_2_ret, add_3_ret, add_5_ret, add_6_ret, add_7_ret;

  Add add_1 (.A(A0), .B(B0), .C(RetE), .Res(Res0), .Ret(add_1_ret));
  Add add_2 (.A(A1), .B(B1), .C(add_1_ret), .Res(Res1), .Ret(add_2_ret));
  Add add_3 (.A(A2), .B(B2), .C(add_2_ret), .Res(Res2), .Ret(add_3_ret));
  Add add_4 (.A(A3), .B(B3), .C(add_3_ret), .Res(Res3), .Ret(RetS));
  Add add_5 (.A(A0_2), .B(B0_2), .C(RetE_2), .Res(Res0_2), .Ret(add_5_ret));
  Add add_6 (.A(A1_2), .B(B1_2), .C(add_5_ret), .Res(Res1_2), .Ret(add_6_ret));
  Add add_7 (.A(A2_2), .B(B2_2), .C(add_6_ret), .Res(Res2_2), .Ret(add_7_ret));
  Add add_8 (.A(A3_2), .B(B3_2), .C(add_7_ret), .Res(Res3_2), .Ret(RetS_2));

  // Notes on the sheet:
  //   Version Réordonnée
endmodule
