// Logisim project boucleIncohérenteCompteur.circ as structural Verilog: 1 circuit, main circuit main
module main (
  input  in_1,
  output out_2,
  output out_3
);

  wire adder_1_cout, adder_2_cout, multiplexer_1_out, multiplexer_2_out;

  Multiplexer #(.enable("false")) multiplexer_1 (.in0(1'b0), .in1(out_2), .out(multiplexer_1_out), .sel(in_1));
  Multiplexer #(.enable("false")) multiplexer_2 (.in0(1'b0), .in1(out_3), .out(multiplexer_2_out), .sel(in_1));
  Adder #(.width(1)) adder_1 (.a(1'b1), .b(multiplexer_1_out), .out(out_2), .cin(1'b0), .cout(adder_1_cout));
  Adder #(.width(1)) adder_2 (.a(1'b0), .b(multiplexer_2_out), .out(out_3), .cin(adder_1_cout), .cout(adder_2_cout));

  // Notes on the sheet:
  //   Simulate/Simulation Enable (off)
  //   Simulate/Reset Simulation
  //   Simulation/Step Simulation (^i)
  //   Quand stable (fin init), mettre entrée à 1 pour observer le bouclage
  //   Comportement souhaité : 00, 01, 10, 11 (...)
endmodule
