// Logisim project euclide.circ as structural Verilog: 1 circuit, main circuit main
module main (
  input  in_1
);

  wire comparator_1_gt, comparator_1_lt;
  wire [7:0] A_q, B_q, multiplexer_1_out, multiplexer_2_out, subtractor_1_out, subtractor_2_out;

  Register A (.D(multiplexer_1_out), .Q(A_q), .clk(in_1));  // open: en, clr
  Register B (.D(multiplexer_2_out), .Q(B_q), .clk(in_1));  // open: en, clr
  Comparator comparator_1 (.a(A_q), .b(B_q), .gt(comparator_1_gt), .lt(comparator_1_lt));  // open: eq
  Subtractor subtractor_1 (.a(A_q), .b(B_q), .out(subtractor_1_out));  // open: bin, bout
  Subtractor subtractor_2 (.a(B_q), .b(A_q), .out(subtractor_2_out));  // open: bin, bout
  Multiplexer #(.width(8)) multiplexer_1 (
    .in0(A_q), .in1(subtractor_1_out), .out(multiplexer_1_out), .sel(comparator_1_gt));  // open: en
  Multiplexer #(.width(8)) multiplexer_2 (
    .in0(B_q), .in1(subtractor_2_out), .out(multiplexer_2_out), .sel(comparator_1_lt));  // open: en

  // Notes on the sheet:
  //   Algorithme d'Euclide
  //   (par exemple avec 8 et 12 (0c) ou avec 9 et -9 (F7))
endmodule
