// Logisim project fibonacciFlot.circ as structural Verilog: 1 circuit, main circuit main
module main (
  input  A5,
  input  A4,
  input  A3,
  input  A2,
  input  A1,
  input  A0,
  input  B5,
  input  B4,
  input  B3,
  input  B2,
  input  B1,
  input  B0,
  output R5,
  output R4,
  output R3,
  output R2,
  output R1,
  output R0,
  output halt
);

  wire Horloge_out, not_1_out, not_2_out, or_1_out;
  wire [4:0] adder_2_out;
  wire [5:0] adder_1_out, multiplexer_1_out, multiplexer_2_out, register_1_q;
  wire [7:0] counter_1_q;

  Clock Horloge (.out(Horloge_out));
  Counter #(.trigger("falling")) counter_1 (.Q(counter_1_q), .clk(Horloge_out));  // open: load, D, count, carry, clr
  or or_1 (or_1_out, counter_1_q[0], counter_1_q[1], counter_1_q[2], counter_1_q[3], counter_1_q[4], counter_1_q[5], counter_1_q[6], counter_1_q[7]);
  not not_1 (not_1_out, or_1_out);
  Multiplexer #(.width(6)) multiplexer_1 (
    .in0({R5, R4, R3, R2, R1, R0}), .in1({A5, A4, A3, A2, A1, A0}), .out(multiplexer_1_out), .sel(not_1_out));  // open: en
  Register #(.width(6)) register_1 (
    .D(multiplexer_1_out), .en(not_2_out), .Q(register_1_q), .clk(Horloge_out));  // open: clr
  Register #(.width(6)) register_2 (
    .D(multiplexer_2_out), .en(not_2_out), .Q({R5, R4, R3, R2, R1, R0}), .clk(Horloge_out));  // open: clr
  Multiplexer #(.width(6)) multiplexer_2 (
    .in0(adder_1_out), .in1({B5, B4, B3, B2, B1, B0}), .out(multiplexer_2_out), .sel(not_1_out));  // open: en
  not not_2 (not_2_out, halt);
  Adder #(.width(6)) adder_1 (.a(register_1_q), .b({R5, R4, R3, R2, R1, R0}), .out(adder_1_out));  // open: cin, cout
  Adder #(.width(6)) adder_2 (
    .a(register_1_q), .b({R5, R4, R3, R2, R1, R0}), .out({halt, adder_2_out}));  // open: cin, cout

  // Notes on the sheet:
  //   Init
  //   fibonacci en flots de données
  //   sortie: plus grand terme possible sur 6 bits
  //   fini?
  //   fini = 1
  //   pas fini = 0
  //   entrée: A et B sur 6 bits en representation C2
  //   A courant
  //   B courant
  //   B = A courant + B courant
  //   A = B courant
  //   prog: tant que A + B >=0 faire:
  //   B=A+B
  //   A=B-A
  //   retourne B
endmodule
