// Logisim project fibonacciPCPO.circ as structural Verilog: 2 circuits, main circuit main
module main (
  input  [7:0] E1,
  input  [7:0] E3,
  input  [7:0] E2,
  input  [7:0] E4,
  output [7:0] S,
  output halt
);

  wire and_1_out, decoder_1_out0, decoder_1_out1, decoder_1_out2, decoder_1_out3, Horloge_out, Init_Boucle_q,
       nor_1_out, not_1_out, or_1_out, or_2_out, ual_1_n, ual_1_z;
  wire [0:0] xor_1_out;
  wire [2:0] bit_extender_1_out;
  wire [2:1] not_2_out;
  wire [7:0] counter_1_q, multiplexer_1_out, multiplexer_2_out, multiplexer_3_out, multiplexer_4_out, R0_q,
       R2_q, R3_q, ual_1_r;

  Clock Horloge (.out(Horloge_out));
  Multiplexer #(.width(8), .enable("false")) multiplexer_1 (
    .in0(multiplexer_2_out), .in1(ual_1_r), .out(multiplexer_1_out), .sel(Init_Boucle_q));
  Decoder #(.select(2), .disabled(0)) decoder_1 (
    .out0(decoder_1_out0), .out1(decoder_1_out1), .out2(decoder_1_out2), .out3(decoder_1_out3),
    .sel({1'b0, xor_1_out[0]}), .en(1'b1));
  or or_1 (or_1_out, Init_Boucle_q, not_2_out[2]);
  not not_1 (not_1_out, not_2_out[2]);
  Counter counter_1 (.Q(counter_1_q), .clk(Horloge_out));  // open: load, D, count, carry, clr
  Register #(.width(1)) Init_Boucle (.D(or_1_out), .Q(Init_Boucle_q), .clk(Horloge_out), .clr(nor_1_out));  // open: en
  Register #(.width(1)) R0_R1 (.D(not_1_out), .Q(not_2_out[2]), .clk(Horloge_out), .clr(nor_1_out));  // open: en
  nor nor_1 (nor_1_out, counter_1_q[0], counter_1_q[1], counter_1_q[2], counter_1_q[3], counter_1_q[4], counter_1_q[5], counter_1_q[6], counter_1_q[7]);
  Bit_Extender #(.out_width(3)) bit_extender_1 (.in(counter_1_q), .out(bit_extender_1_out));
  and and_1 (and_1_out, counter_1_q[0], counter_1_q[1], counter_1_q[2], counter_1_q[3], counter_1_q[4], counter_1_q[5], counter_1_q[6], counter_1_q[7]);
  Register R0 (.D(multiplexer_1_out), .en(decoder_1_out0), .Q(R0_q), .clk(Horloge_out));  // open: clr
  Multiplexer #(.select(3), .width(8), .enable("false")) multiplexer_2 (
    .in1(E1), .in2(E2), .in3(E3), .in4(E4), .out(multiplexer_2_out), .sel(bit_extender_1_out));  // open: in0, in5, in6, in7
  Register R1 (.D(multiplexer_1_out), .en(decoder_1_out1), .Q(S), .clk(Horloge_out));  // open: clr
  Register R3 (.D(multiplexer_1_out), .en(decoder_1_out3), .Q(R3_q), .clk(Horloge_out));  // open: clr
  Register R2 (.D(multiplexer_1_out), .en(decoder_1_out2), .Q(R2_q), .clk(Horloge_out));  // open: clr
  xor xor_1 (xor_1_out[0], Init_Boucle_q, not_2_out[2]);
  Multiplexer #(.select(2), .width(8), .enable("false")) multiplexer_3 (
    .in0(R0_q), .in1(S), .in2(R2_q), .in3(R3_q), .out(multiplexer_3_out), .sel(2'b01));
  UAL ual_1 (
    .Op0(multiplexer_3_out), .Op1(multiplexer_4_out), .R(ual_1_r), .Fun({not_2_out, not_2_out[1]}),
    .N(ual_1_n), .Z(ual_1_z));
  Multiplexer #(.select(2), .width(8), .enable("false")) multiplexer_4 (
    .in0(R0_q), .in1(S), .in2(R2_q), .in3(R3_q), .out(multiplexer_4_out), .sel(2'b00));
  not not_2 (not_2_out[1], not_2_out[2]);
  and and_2 (halt, Init_Boucle_q, or_2_out);
  or or_2 (or_2_out, and_1_out, ual_1_r[7]);

  // Notes on the sheet:
  //   H
  //   E
  //   I
  //   Z
  //   Compteur
  //   Temps
  //   N
  //   Init (Temps 0)
  //   Fibonacci : Un = Un-1 + Un-2
  //   R0 <= Entrée ; R1 <= Entrée
  //   tant que  R0+R1 > 0 : 
  //   R1 <= R1 + R0
  //   R0 <= R1 - R0
  //   Entree (courante)
  //   D
  //   Ecr
  //   Fournir 4 Entrees (poids faible d'abord)
  //   Temps 0 : Init
  //   Temps 1 : 1ere Entree
  //   Temps 2 : 2e Entree
  //   etc
  //   Temps 255 : Halt
  //   Reg
  //   Op1
  //   Activer l'horloge (manuellement ou automatiquement)
  //   Fun
  //   Op0
  //   UAL
endmodule

module UAL (
  input  [7:0] Op0,
  input  [7:0] Op1,
  input  [2:0] Fun,
  output [7:0] R,
  output N,
  output Z
);

  wire [7:0] adder_1_out, and_1_out, not_1_out, or_1_out, shifter_1_out, subtractor_1_out, xor_1_out;

  assign not_1_out = ~Op0;  // NOT_Gate not_1, 8 bits wide
  Shifter #(.shift("ar")) shifter_1 (.in(Op0), .\dist (3'b001), .out(shifter_1_out));
  Adder adder_1 (.a(Op0), .b(Op1), .out(adder_1_out), .cin(1'b0));  // open: cout
  Subtractor subtractor_1 (.a(Op0), .b(Op1), .out(subtractor_1_out), .bin(1'b0));  // open: bout
  assign and_1_out = Op0 & Op1;  // AND_Gate and_1, 8 bits wide
  assign or_1_out = Op0 | Op1;  // OR_Gate or_1, 8 bits wide
  assign xor_1_out = Op0 ^ Op1;  // XOR_Gate xor_1, 8 bits wide
  Multiplexer #(.select(3), .width(8), .enable("false")) multiplexer_1 (
    .in0(Op0), .in1(not_1_out), .in2(shifter_1_out), .in3(adder_1_out), .in4(subtractor_1_out),
    .in5(and_1_out), .in6(or_1_out), .in7(xor_1_out), .out({N, R[6:0]}), .sel(Fun));
  nor nor_1 (Z, N, R[6], R[5], R[4], R[3], R[2], R[1], R[0]);

  assign R[7] = N;
endmodule
