// Logisim project mult.circ as structural Verilog: 2 circuits, main circuit main
module main (
  input  RIN,
  input  AIN,
  input  BIN,
  input  CIN,
  output BOUT,
  output COUT,
  output AOUT,
  output ROUT
);

  wire and_1_out, and_2_out, and_3_out, and_4_out, and_5_out, and_6_out, and_7_out, and_8_out, and_9_out,
       not_1_out, not_2_out, not_3_out, not_4_out;

  or or_1 (COUT, and_1_out, and_2_out, and_3_out);
  and and_1 (and_1_out, RIN, CIN);
  and and_2 (and_2_out, RIN, AIN, BIN);
  and and_3 (and_3_out, CIN, AIN, BIN);
  and and_4 (and_4_out, not_3_out, not_1_out, CIN);
  and and_5 (and_5_out, not_3_out, RIN, not_4_out);
  or or_2 (ROUT, and_4_out, and_5_out, and_6_out, and_7_out, and_8_out, and_9_out);
  not not_1 (not_1_out, RIN);
  not not_2 (not_2_out, AIN);
  and and_6 (and_6_out, not_2_out, not_1_out, CIN);
  not not_3 (not_3_out, BIN);
  and and_7 (and_7_out, not_2_out, RIN, not_4_out);
  and and_8 (and_8_out, AIN, BIN, not_1_out, not_4_out);
  not not_4 (not_4_out, CIN);
  and and_9 (and_9_out, AIN, BIN, RIN, CIN);

  assign AOUT = AIN;
  assign BOUT = BIN;

  // Notes on the sheet:
  //   Cellule de multiplication
endmodule

module mult4 (
  input  A3,
  input  in_2,
  input  in_3,
  input  A0,
  input  in_5,
  input  B0,
  input  in_7,
  input  in_8,
  input  B3,
  output out_10,
  output out_11,
  output out_12,
  output out_13,
  output out_14,
  output out_15,
  output out_16,
  output out_17,
  output out_18,
  output out_19,
  output out_20,
  output R0,
  output out_22,
  output out_23,
  output out_24,
  output out_25
);

  wire main_2_aout, main_2_cout, main_2_rout, main_3_bout, main_3_cout, main_4_aout, main_4_cout,
       main_4_rout, main_5_aout, main_5_cout, main_5_rout, main_6_aout, main_6_bout, main_6_cout,
       main_6_rout, main_7_aout, main_7_bout, main_7_cout, main_7_rout, main_8_aout, main_8_bout,
       main_8_cout, main_8_rout, main_9_bout, main_9_cout, main_10_bout, main_10_cout, main_11_aout,
       main_11_bout, main_11_cout, main_11_rout, main_12_aout, main_12_bout, main_12_cout, main_12_rout,
       main_13_aout, main_13_bout, main_13_cout, main_14_aout, main_14_bout, main_14_cout, main_14_rout,
       main_15_aout, main_15_bout, main_15_cout, main_16_aout, main_16_bout, main_16_cout;

  main main_1 (
    .BOUT(out_13), .COUT(out_14), .ROUT(out_15), .BIN(main_3_bout), .CIN(main_3_cout), .RIN(main_2_cout),
    .AIN(main_2_aout), .AOUT(out_22));
  main main_2 (
    .BOUT(out_12), .COUT(main_2_cout), .ROUT(main_2_rout), .BIN(main_7_bout), .CIN(main_7_cout),
    .RIN(main_5_cout), .AIN(main_5_aout), .AOUT(main_2_aout));
  main main_3 (
    .BOUT(main_3_bout), .COUT(main_3_cout), .ROUT(out_16), .BIN(main_10_bout), .CIN(main_10_cout),
    .RIN(main_2_rout), .AIN(main_7_aout), .AOUT(out_23));
  main main_4 (
    .BOUT(out_10), .COUT(main_4_cout), .ROUT(main_4_rout), .BIN(main_11_bout), .CIN(main_11_cout),
    .RIN(in_5), .AIN(A3), .AOUT(main_4_aout));
  main main_5 (
    .BOUT(out_11), .COUT(main_5_cout), .ROUT(main_5_rout), .BIN(main_6_bout), .CIN(main_6_cout),
    .RIN(main_4_cout), .AIN(main_4_aout), .AOUT(main_5_aout));
  main main_6 (
    .BOUT(main_6_bout), .COUT(main_6_cout), .ROUT(main_6_rout), .BIN(main_12_bout), .CIN(main_12_cout),
    .RIN(main_4_rout), .AIN(main_11_aout), .AOUT(main_6_aout));
  main main_7 (
    .BOUT(main_7_bout), .COUT(main_7_cout), .ROUT(main_7_rout), .BIN(main_8_bout), .CIN(main_8_cout),
    .RIN(main_5_rout), .AIN(main_6_aout), .AOUT(main_7_aout));
  main main_8 (
    .BOUT(main_8_bout), .COUT(main_8_cout), .ROUT(main_8_rout), .BIN(main_13_bout), .CIN(main_13_cout),
    .RIN(main_6_rout), .AIN(main_12_aout), .AOUT(main_8_aout));
  main main_9 (
    .BOUT(main_9_bout), .COUT(main_9_cout), .ROUT(out_18), .BIN(B3), .CIN(in_5), .RIN(main_8_rout),
    .AIN(main_13_aout), .AOUT(out_25));
  main main_10 (
    .BOUT(main_10_bout), .COUT(main_10_cout), .ROUT(out_17), .BIN(main_9_bout), .CIN(main_9_cout),
    .RIN(main_7_rout), .AIN(main_8_aout), .AOUT(out_24));
  main main_11 (
    .BOUT(main_11_bout), .COUT(main_11_cout), .ROUT(main_11_rout), .BIN(main_14_bout), .CIN(main_14_cout),
    .RIN(in_5), .AIN(in_2), .AOUT(main_11_aout));
  main main_12 (
    .BOUT(main_12_bout), .COUT(main_12_cout), .ROUT(main_12_rout), .BIN(main_15_bout), .CIN(main_15_cout),
    .RIN(main_11_rout), .AIN(main_14_aout), .AOUT(main_12_aout));
  main main_13 (
    .BOUT(main_13_bout), .COUT(main_13_cout), .ROUT(out_19), .BIN(in_8), .CIN(in_5), .RIN(main_12_rout),
    .AIN(main_15_aout), .AOUT(main_13_aout));
  main main_14 (
    .BOUT(main_14_bout), .COUT(main_14_cout), .ROUT(main_14_rout), .BIN(main_16_bout), .CIN(main_16_cout),
    .RIN(in_5), .AIN(in_3), .AOUT(main_14_aout));
  main main_15 (
    .BOUT(main_15_bout), .COUT(main_15_cout), .ROUT(out_20), .BIN(in_7), .CIN(in_5), .RIN(main_14_rout),
    .AIN(main_16_aout), .AOUT(main_15_aout));
  main main_16 (
    .BOUT(main_16_bout), .COUT(main_16_cout), .ROUT(R0), .BIN(B0), .CIN(in_5), .RIN(in_5), .AIN(A0),
    .AOUT(main_16_aout));

  // Notes on the sheet:
  //   R7
  //   R (8bits) <= A (4 bits) * B (4 bits)
endmodule
