// Logisim project mux248.circ as structural Verilog: 4 circuits, main circuit main
module main (
);


  // Notes on the sheet:
  //   Multiplexeurs
  //   Mux8 : ébauche de multiplexeur 8 (+3) => 1 à partir de Mux4
  //   Mux2 : multiplexeur de base [porte logique élémentaire], en entrée : 2 bits (+1 bit de commande) => en sortie : 1 bit.
  //    Mux4 : multiplexeur avec en entrée 4 bits (+2 bits de commande) => en sortie 1 bit. Circuit réalisé à partir de Mux2 (c. prec.)
endmodule

module mux2 (
  input  C,
  input  E1,
  input  E0,
  output X
);

  wire and_1_out, and_2_out, not_1_out;

  and and_1 (and_1_out, C, E1);
  not not_1 (not_1_out, C);
  and and_2 (and_2_out, not_1_out, E0);
  or or_1 (X, and_1_out, and_2_out);
endmodule

module mux4 (
  input  Cfaible,
  input  CFort,
  input  E11,
  input  E01,
  input  E10,
  input  E00,
  output XX
);

  wire mux2_1_x, mux2_2_x;

  mux2 mux2_1 (.E1(E11), .E0(E01), .C(CFort), .X(mux2_1_x));
  mux2 mux2_2 (.E1(E10), .E0(E00), .C(CFort), .X(mux2_2_x));
  mux2 mux2_3 (.E1(mux2_1_x), .E0(mux2_2_x), .C(Cfaible), .X(XX));
endmodule

module mux8 (
);

  wire mux2_1_x, mux4_1_xx, mux4_2_xx, undriven, undriven_2, undriven_3, undriven_4, undriven_5, undriven_6,
       undriven_7, undriven_8, undriven_9, undriven_10, undriven_11;

  mux4 mux4_1 (
    .Cfaible(undriven_10), .E11(undriven), .E01(undriven_2), .E10(undriven_3), .E00(undriven_4),
    .XX(mux4_1_xx), .CFort(undriven_9));
  mux4 mux4_2 (
    .Cfaible(undriven_10), .E11(undriven_5), .E01(undriven_6), .E10(undriven_7), .E00(undriven_8),
    .XX(mux4_2_xx), .CFort(undriven_9));
  mux2 mux2_1 (.E1(mux4_1_xx), .E0(mux4_2_xx), .C(undriven_11), .X(mux2_1_x));
endmodule
