// Logisim project nonEt.circ as structural Verilog: 1 circuit, main circuit main
module main (
  input  A,
  input  B,
  output S
);

  wire transistor_3_out;

  Transistor transistor_1 (.in(1'b1), .out(S), .gate(A));
  Transistor #(.\type ("n")) transistor_2 (.in(transistor_3_out), .out(S), .gate(A));
  Transistor #(.\type ("n"), .gate("br")) transistor_3 (.in(1'b0), .out(transistor_3_out), .gate(B));
  Transistor #(.gate("br")) transistor_4 (.in(1'b1), .out(S), .gate(B));
endmodule
