// Logisim project processeurJouet.circ as structural Verilog: 4 circuits, main circuit main
module main (
  input  [7:0] E1,
  input  [7:0] E3,
  input  [7:0] E2,
  input  [7:0] E4,
  output [7:0] S,
  output halt
);

  wire and_1_out, and_3_out, and_4_out, and_5_out, and_6_out, and_7_out, and_8_out, and_9_out, and_10_out,
       and_11_out, and_12_out, decoder_1_out0, decoder_1_out1, decoder_1_out2, decoder_1_out3, Horloge_out,
       nor_1_out, or_1_out, or_2_out, or_3_out, or_4_out, ual_1_n, ual_1_z;
  wire [1:0] multiplexer_9_out_2, multiplexer_9_out_3, multiplexer_9_out_5, multiplexer_9_out_6,
       multiplexer_9_out_7, multiplexer_9_out_8;
  wire [2:0] bit_extender_1_out, multiplexer_9_out_4;
  wire [3:0] E0_q;
  wire [7:0] Adr_q, counter_1_q, Data_q, multiplexer_1_out, multiplexer_2_out, multiplexer_3_out,
       multiplexer_4_out, multiplexer_5_out, multiplexer_6_out, multiplexer_7_out, multiplexer_8_out,
       multiplexer_9_out_9, PC_q, pcl_1_r, R1_q, R2_q, R3_q, ram_1_data, RI_q, rom_1_data, ual_1_r;
  wire [21:0] multiplexer_9_out;
  wire [31:1] undriven_2, undriven_3, undriven_4, undriven_5, undriven_7, undriven_8;
  wire [31:6] undriven, undriven_6;

  Clock Horloge (.out(Horloge_out));
  Multiplexer #(.select(2), .width(8), .enable("false")) multiplexer_1 (
    .in0(multiplexer_5_out), .in1(multiplexer_2_out), .in2(multiplexer_9_out_9), .in3(ual_1_r),
    .out(multiplexer_1_out), .sel(multiplexer_9_out_8));
  Decoder #(.select(2), .disabled(0)) decoder_1 (
    .out0(decoder_1_out0), .out1(decoder_1_out1), .out2(decoder_1_out2), .out3(decoder_1_out3),
    .sel(multiplexer_9_out_7), .en(multiplexer_9_out[21]));
  Register #(.width(1)) u_E3 (.D(and_3_out), .Q(E0_q[3]), .clk(Horloge_out), .clr(nor_1_out));  // open: en
  Register #(.width(1)) u_E2 (.D(or_2_out), .Q(E0_q[2]), .clk(Horloge_out), .clr(nor_1_out));  // open: en
  Register #(.width(1)) u_E1 (.D(or_3_out), .Q(E0_q[1]), .clk(Horloge_out), .clr(nor_1_out));  // open: en
  Register #(.width(1)) E0 (.D(or_4_out), .Q(E0_q[0]), .clk(Horloge_out), .clr(nor_1_out));  // open: en
  Counter counter_1 (.Q(counter_1_q), .clk(Horloge_out));  // open: load, D, count, carry, clr
  Register R0 (.D(multiplexer_1_out), .en(decoder_1_out0), .Q(S), .clk(Horloge_out));  // open: clr
  and and_1 (and_1_out, counter_1_q[0], counter_1_q[2]);
  nor nor_1 (nor_1_out, counter_1_q[0], counter_1_q[1], counter_1_q[2], counter_1_q[3], counter_1_q[4], counter_1_q[5], counter_1_q[6], counter_1_q[7]);
  Bit_Extender #(.out_width(3)) bit_extender_1 (.in(counter_1_q), .out(bit_extender_1_out));
  and and_2 (halt, counter_1_q[0], counter_1_q[1], counter_1_q[2], counter_1_q[3], counter_1_q[4], counter_1_q[5], counter_1_q[6], counter_1_q[7]);
  Register R1 (.D(multiplexer_1_out), .en(decoder_1_out1), .Q(R1_q), .clk(Horloge_out));  // open: clr
  Multiplexer #(.select(3), .width(8), .enable("false")) multiplexer_2 (
    .in1(E1), .in2(E2), .in3(E3), .in4(E4), .out(multiplexer_2_out), .sel(bit_extender_1_out));  // open: in0, in5, in6, in7
  Register R2 (.D(multiplexer_1_out), .en(decoder_1_out2), .Q(R2_q), .clk(Horloge_out));  // open: clr
  and and_3 (and_3_out, ~E0_q[3], E0_q[2], E0_q[1], ~E0_q[0]);  // AND_Gate
  and and_4 (and_4_out, multiplexer_6_out[2], ~E0_q[3], E0_q[2], ~E0_q[1], ~E0_q[0]);  // AND_Gate
  and and_5 (and_5_out, multiplexer_6_out[1], ~E0_q[3], E0_q[2], ~E0_q[1], ~E0_q[0]);  // AND_Gate
  or or_1 (or_1_out, multiplexer_6_out[1], multiplexer_6_out[2]);
  and and_6 (and_6_out, or_1_out, ~E0_q[3], ~E0_q[2], ~E0_q[1], E0_q[0]);  // AND_Gate
  and and_7 (and_7_out, ~E0_q[3], ~E0_q[2], ~E0_q[1], E0_q[0], multiplexer_6_out[0]);  // AND_Gate
  and and_8 (and_8_out, ~E0_q[1], ~E0_q[2], ~E0_q[3], E0_q[0], multiplexer_6_out[3]);  // AND_Gate
  and and_9 (and_9_out, E0_q[3], ~E0_q[2], ~E0_q[1], ~E0_q[0]);  // AND_Gate
  and and_10 (and_10_out, ~E0_q[3], E0_q[2], ~E0_q[1], E0_q[0]);  // AND_Gate
  and and_11 (and_11_out, ~E0_q[3], ~E0_q[2], ~E0_q[1], ~E0_q[0], and_1_out);  // AND_Gate
  and and_12 (and_12_out, ~E0_q[3], ~E0_q[2], E0_q[1]);  // AND_Gate
  Register R3 (.D(multiplexer_1_out), .en(decoder_1_out3), .Q(R3_q), .clk(Horloge_out));  // open: clr
  or or_2 (or_2_out, and_4_out, and_5_out, and_6_out);
  or or_3 (or_3_out, and_4_out, and_7_out, and_8_out);
  or or_4 (or_4_out, and_5_out, and_8_out, and_9_out, and_10_out, and_11_out, and_12_out);
  Multiplexer #(.select(2), .width(8), .enable("false")) multiplexer_3 (
    .in0(S), .in1(R1_q), .in2(R2_q), .in3(R3_q), .out(multiplexer_3_out), .sel(multiplexer_9_out_6));
  PCL pcl_1 (.in_1(PC_q), .in_2(multiplexer_1_out), .R(pcl_1_r), .Sel(multiplexer_9_out[11]));
  UAL ual_1 (
    .Op0(multiplexer_3_out), .Op1(multiplexer_4_out), .R(ual_1_r), .Fun(multiplexer_9_out_4), .N(ual_1_n),
    .Z(ual_1_z));
  Multiplexer #(.select(2), .width(8), .enable("false")) multiplexer_4 (
    .in0(S), .in1(R1_q), .in2(R2_q), .in3(R3_q), .out(multiplexer_4_out), .sel(multiplexer_9_out_5));
  Multiplexer #(.select(2), .width(8), .enable("false")) multiplexer_5 (
    .in0(ram_1_data), .in1(rom_1_data), .in2(Adr_q), .in3(PC_q), .out(multiplexer_5_out),
    .sel(multiplexer_9_out_3));
  Register PC (.D(pcl_1_r), .en(multiplexer_9_out[10]), .Q(PC_q), .clk(Horloge_out));  // open: clr
  Register RI (.D(multiplexer_1_out), .en(multiplexer_9_out[7]), .Q(RI_q), .clk(Horloge_out));  // open: clr
  Multiplexer #(.width(8), .enable("false")) multiplexer_6 (
    .in0(RI_q), .in1(multiplexer_1_out), .out(multiplexer_6_out), .sel(multiplexer_9_out[6]));
  Register Adr (.D(multiplexer_1_out), .en(multiplexer_9_out[5]), .Q(Adr_q), .clk(Horloge_out));  // open: clr
  Register Data (.D(multiplexer_1_out), .en(multiplexer_9_out[4]), .Q(Data_q), .clk(Horloge_out));  // open: clr
  Multiplexer #(.select(2), .width(8), .enable("false")) multiplexer_7 (
    .in0(Adr_q), .in1(PC_q), .in2(multiplexer_1_out), .in3(ual_1_r), .out(multiplexer_7_out),
    .sel(multiplexer_9_out_2));
  Multiplexer #(.width(8), .enable("false")) multiplexer_8 (
    .in0(ual_1_r), .in1(Data_q), .out(multiplexer_8_out), .sel(multiplexer_9_out[1]));
  ROM rom_1 (.addr(multiplexer_7_out), .data(rom_1_data), .sel(1'b1));
  RAM #(.bus("separate")) ram_1 (
    .addr(multiplexer_7_out), .din(multiplexer_8_out), .data(ram_1_data), .str(multiplexer_9_out[0]),
    .sel(1'b1), .clk(Horloge_out), .ld(1'b1));  // open: clr
  Multiplexer #(.select(4), .width(32), .enable("false")) multiplexer_9 (
    .in0({undriven[31:24], 3'b010, undriven[20:12], 2'b01, undriven[9:8], 1'b0, undriven[6], 6'b010111}),
    .in1({undriven_2[31:24], 3'b000, undriven_2[20:12], 10'h171, undriven_2[1], 1'b0}),
    .in2({undriven_3[31:24], 5'b00100, undriven_3[18:12], 5'b01010, undriven_3[6], 4'b0001, undriven_3[1], 1'b0}),
    .in3({undriven_4[31:24], 3'b000, undriven_4[20:12], 5'b11010, undriven_4[6], 4'b0001, undriven_4[1], 1'b0}),
    .in4({undriven_5[31:24], 3'b000, undriven_5[20:12], 10'h149, undriven_5[1], 1'b0}),
    .in5({undriven_6[31:22], 1'b0, undriven_6[20:19], 7'b0000101, undriven_6[11], 1'b0, undriven_6[9:8], 1'b0, undriven_6[6], 6'b000001}),
    .in6({undriven_7[31:24], 5'b00101, undriven_7[18:11], 4'b0000, undriven_7[6], 4'b0000, undriven_7[1], 1'b0}),
    .in8({undriven_8[31:24], 12'he0b, undriven_8[11], 1'b0, undriven_8[9:8], 1'b0, undriven_8[6], 2'b00, undriven_8[3:1], 1'b0}),
    .out({multiplexer_9_out_9, multiplexer_9_out_8, multiplexer_9_out[21], multiplexer_9_out_7, multiplexer_9_out_6, multiplexer_9_out_5, multiplexer_9_out_4, multiplexer_9_out[11:10], multiplexer_9_out_3, multiplexer_9_out[7:4], multiplexer_9_out_2, multiplexer_9_out[1:0]}),
    .sel(E0_q));  // open: in7, in9, in10, in11, in12, in13, in14, in15

  // Notes on the sheet:
  //   H
  //   E
  //   I
  //   Compteur
  //   Temps
  //   E3 2 1 0
  //   Init (Temps 0)
  //   Z
  //   N
  //   (6)
  //   (4&V2)
  //   (4&V1)
  //   (1&(V1|V2))
  //   (1&V0)
  //   (1&V3)
  //   (8)
  //   (5)
  //   (0&Fi)
  //   (2|3)
  //   Entree (courante)
  //   Op0
  //   Reg
  //   Ecr
  //   ERM
  //   V
  //   Fun
  //   UAL
  //   Op1
  //   Temps 0 : Init
  //   etc
  //   Temps 255 : Halt
  //   EcrPc
  //   PcL
  //   0
  //   4
  //   8
  //   Fournir 4 Entrees (8 bits)
  //   Temps 1 : 1ere Entree, enregistree en RAM[@02]
  //   Temps 2 : 2e Entree, enregistree en RAM[@03]
  //   RR
  //   EcrRI
  //   MPA
  //   Activer l'horloge (manuellement ou automatiquement)
  //   EcrD
  //   EcrA
  //   ROM
  //   RAM
  //   SD
  //   PcAR
  //   Debut du prog. ROM[@06]
  //   EcrM
  //   contents of rom_1 (hex, n*v repeats v):
  //   6*0 1 0 4 2 4 3 8 c 0 0 1 1 2 3 4 5 6 7 8 9 a 6*0 2 4 6 8 a c e 10 12 14 6*0 3 6 9 c f 12 15 18 1b
  //   1e 6*0 4 8 c 10 14 18 1c 20 24 28 6*0 5 a f 14 19 1e 23 28 2d 32 6*0 6 c 12 18 1e 24 2a 30 36 3c 6*0
  //   7 e 15 1c 23 2a 31 38 3f 46 6*0 8 10 18 20 28 30 38 40 48 50 6*0 9 12 1b 24 2d 36 3f 48 51 5a 6*0 a
  //   14 1e 28 32 3c 46 50 5a 64 53*0 1 10 4 ff 8 e2
endmodule

module UAL (
  input  [7:0] Op0,
  input  [7:0] Op1,
  input  [2:0] Fun,
  output [7:0] R,
  output N,
  output Z
);

  wire [7:0] adder_1_out, adder_2_out, and_1_out, not_1_out, or_1_out, shifter_1_out, subtractor_1_out,
       xor_1_out;

  Adder adder_1 (.a(8'h1), .b(Op0), .out(adder_1_out), .cin(1'b0));  // open: cout
  assign not_1_out = ~Op0;  // NOT_Gate not_1, 8 bits wide
  Shifter #(.shift("ar")) shifter_1 (.in(Op0), .\dist (3'b001), .out(shifter_1_out));
  Adder adder_2 (.a(Op0), .b(Op1), .out(adder_2_out), .cin(1'b0));  // open: cout
  Subtractor subtractor_1 (.a(Op0), .b(Op1), .out(subtractor_1_out), .bin(1'b0));  // open: bout
  assign and_1_out = Op0 & Op1;  // AND_Gate and_1, 8 bits wide
  assign or_1_out = Op0 | Op1;  // OR_Gate or_1, 8 bits wide
  assign xor_1_out = Op0 ^ Op1;  // XOR_Gate xor_1, 8 bits wide
  Multiplexer #(.select(3), .width(8), .enable("false")) multiplexer_1 (
    .in0(adder_1_out), .in1(not_1_out), .in2(shifter_1_out), .in3(adder_2_out), .in4(subtractor_1_out),
    .in5(and_1_out), .in6(or_1_out), .in7(xor_1_out), .out({N, R[6:0]}), .sel(Fun));
  nor nor_1 (Z, N, R[6], R[5], R[4], R[3], R[2], R[1], R[0]);

  assign R[7] = N;
endmodule

module PCL (
  input  [7:0] in_1,
  input  [7:0] in_2,
  input  Sel,
  output [7:0] R
);

  wire [7:0] adder_1_out;

  Adder adder_1 (.a(in_1), .b({8{1'b0}}), .out(adder_1_out), .cin(1'b1));  // open: cout
  Multiplexer #(.width(8), .enable("false")) multiplexer_1 (.in0(adder_1_out), .in1(in_2), .out(R), .sel(Sel));
endmodule

module tmp (
);

  wire register_1_q, ual_1_z, undriven_3, undriven_4;
  wire [7:0] ual_1_r, undriven, undriven_2;

  UAL ual_1 (.Op0(undriven), .Op1(undriven_2), .R(ual_1_r), .Z(ual_1_z));  // open: Fun, N
  Register #(.width(1)) register_1 (.D(ual_1_z), .en(undriven_3), .Q(register_1_q), .clk(undriven_4));  // open: clr

  // Notes on the sheet:
  //   Op1
  //   Op2
  //   Res
  //   N
  //   H
  //   N
  //   EcrN
  //   MemN
endmodule
