// Logisim project syracuseBitABitTrancheEtTotal.circ as structural Verilog: 3 circuits, main circuit main
module main (
);

  wire adder_1_cout, adder_1_out, adder_2_cout, adder_2_out, adder_3_cout, adder_3_out, adder_4_out,
       clock_1_out, multiplexer_1_out, multiplexer_2_out, multiplexer_3_out, multiplexer_4_out, undriven;
  wire [3:0] register_1_q;

  Clock clock_1 (.out(clock_1_out));
  Register #(.width(1), .trigger("falling")) register_1 (
    .D(multiplexer_1_out), .Q(register_1_q[0]), .clk(clock_1_out));  // open: en, clr
  Register #(.width(1), .trigger("falling")) register_2 (
    .D(multiplexer_2_out), .Q(register_1_q[1]), .clk(clock_1_out));  // open: en, clr
  Register #(.width(1), .trigger("falling")) register_3 (
    .D(multiplexer_3_out), .Q(register_1_q[2]), .clk(clock_1_out));  // open: en, clr
  Register #(.width(1), .trigger("falling")) register_4 (
    .D(multiplexer_4_out), .Q(register_1_q[3]), .clk(clock_1_out));  // open: en, clr
  Hex_Digit_Display hex_digit_display_1 (.value(register_1_q));  // open: dp
  Adder #(.width(1)) adder_1 (.a(register_1_q[0]), .b(1'b0), .out(adder_1_out), .cin(1'b1), .cout(adder_1_cout));
  Adder #(.width(1)) adder_2 (
    .a(register_1_q[1]), .b(register_1_q[0]), .out(adder_2_out), .cin(adder_1_cout), .cout(adder_2_cout));
  Adder #(.width(1)) adder_3 (
    .a(register_1_q[2]), .b(register_1_q[1]), .out(adder_3_out), .cin(adder_2_cout), .cout(adder_3_cout));
  Adder #(.width(1)) adder_4 (
    .a(register_1_q[3]), .b(register_1_q[2]), .out(adder_4_out), .cin(adder_3_cout));  // open: cout
  Multiplexer #(.enable("false")) multiplexer_1 (
    .in0(register_1_q[1]), .in1(adder_1_out), .out(multiplexer_1_out), .sel(register_1_q[0]));
  Multiplexer #(.enable("false")) multiplexer_2 (
    .in0(register_1_q[2]), .in1(adder_2_out), .out(multiplexer_2_out), .sel(register_1_q[0]));
  Multiplexer #(.enable("false")) multiplexer_3 (
    .in0(register_1_q[3]), .in1(adder_3_out), .out(multiplexer_3_out), .sel(register_1_q[0]));
  Multiplexer #(.enable("false")) multiplexer_4 (
    .in0(undriven), .in1(adder_4_out), .out(multiplexer_4_out), .sel(register_1_q[0]));

  // Notes on the sheet:
  //    version C2 si duplication (haut)
  //   version BP si on relie 0
  //   Suite de Syracuse (sur 4 bits)
  //   Si V pair :
  //   Sinon :
  //   V <<== V / 2
  //   V <<==  3 * V + 1
  //   Numération :   Binaire pur :    Complément à 2
  //    0 0 0 0 (0) :             0     :                  0
  //    0 0 0 1 (1) :             1     :                  1
  //    0 0 1 0 (2) :             2     :                  2
  //    0 0 1 1 (3) :             3     :                  3
  //    0 1 0 0 (4) :             4     :                  4
  //    0 1 0 1 (5)  :             5     :                  5
  //    0 1 0 1 (6) :             6     :                  6
  //    0 1 1 1 (7)  :             7     :                  7
  //    1 0 0 0 (8) :             8     :                  -8
  //    1 0 0 1 (9) :             9     :                  -7
  //    1 0 1 0 (A) :             10    :                  -6
  //    1 0 1 1 (b) :             11    :                  -5
  //    1 1 0 0 (C) :             12    :                  -4
  //    1 1 0 1 (d)  :             13    :                  -3
  //    1 1 0 1 (E) :             14    :                  -2
  //    1 1 1 1 (F)  :             15    :                  -1
endmodule

module tranche (
);

  wire adder_1_cout, adder_1_out, multiplexer_1_out, register_1_q, undriven, undriven_2, undriven_3,
       undriven_4, undriven_5;

  Register #(.width(1), .trigger("falling")) register_1 (
    .D(multiplexer_1_out), .Q(register_1_q), .clk(undriven));  // open: en, clr
  Adder #(.width(1)) adder_1 (
    .a(register_1_q), .b(undriven_2), .out(adder_1_out), .cin(undriven_4), .cout(adder_1_cout));
  Multiplexer #(.enable("false")) multiplexer_1 (
    .in0(undriven_3), .in1(adder_1_out), .out(multiplexer_1_out), .sel(undriven_5));

  // Notes on the sheet:
  //   *2
  //   /2
endmodule

module brouillon (
);

  wire adder_1_cout, adder_1_out, adder_2_cout, adder_2_out, adder_3_cout, adder_3_out, adder_4_cout,
       adder_4_out, clock_1_out, multiplexer_1_out, multiplexer_2_out, multiplexer_3_out, multiplexer_4_out,
       register_1_q, register_2_q, register_3_q, register_4_q;

  Clock clock_1 (.out(clock_1_out));
  Register #(.width(1), .trigger("falling")) register_1 (
    .D(multiplexer_1_out), .Q(register_1_q), .clk(clock_1_out));  // open: en, clr
  Register #(.width(1), .trigger("falling")) register_2 (
    .D(multiplexer_2_out), .Q(register_2_q), .clk(clock_1_out));  // open: en, clr
  Register #(.width(1), .trigger("falling")) register_3 (
    .D(multiplexer_3_out), .Q(register_3_q), .clk(clock_1_out));  // open: en, clr
  Register #(.width(1), .trigger("falling")) register_4 (
    .D(multiplexer_4_out), .Q(register_4_q), .clk(clock_1_out));  // open: en, clr
  Adder #(.width(1)) adder_1 (.a(register_1_q), .b(1'b0), .out(adder_1_out), .cin(1'b1), .cout(adder_1_cout));
  Adder #(.width(1)) adder_2 (
    .a(register_2_q), .b(register_1_q), .out(adder_2_out), .cin(adder_1_cout), .cout(adder_2_cout));
  Adder #(.width(1)) adder_3 (
    .a(register_3_q), .b(register_2_q), .out(adder_3_out), .cin(adder_2_cout), .cout(adder_3_cout));
  Adder #(.width(1)) adder_4 (
    .a(register_4_q), .b(register_3_q), .out(adder_4_out), .cin(adder_3_cout), .cout(adder_4_cout));
  Multiplexer #(.enable("false")) multiplexer_1 (
    .in0(register_2_q), .in1(adder_1_out), .out(multiplexer_1_out), .sel(register_1_q));
  Multiplexer #(.enable("false")) multiplexer_2 (
    .in0(register_3_q), .in1(adder_2_out), .out(multiplexer_2_out), .sel(register_1_q));
  Multiplexer #(.enable("false")) multiplexer_3 (
    .in0(register_4_q), .in1(adder_3_out), .out(multiplexer_3_out), .sel(register_1_q));
  Multiplexer #(.enable("false")) multiplexer_4 (
    .in0(register_4_q), .in1(adder_4_out), .out(multiplexer_4_out), .sel(register_1_q));

  // Notes on the sheet:
  //   *2
  //   *2
  //   *2
  //   *2
  //   /2
  //   /2
  //   /2
  //   /2
  //   Suite de Syracuse (sur 4 bits)
  //   Si V pair :
  //   V <<== V / 2
  //   V <<==  3 * V + 1
endmodule
