// Logisim project syracuseFlot.circ as structural Verilog: 1 circuit, main circuit main
module main (
);

  wire clock_1_out;
  wire [3:0] adder_1_out, multiplexer_1_out, register_1_q, shifter_1_out, shifter_2_out;

  Hex_Digit_Display hex_digit_display_1 (.value(register_1_q));  // open: dp
  Register #(.width(4)) register_1 (.D(multiplexer_1_out), .Q(register_1_q), .clk(clock_1_out));  // open: en, clr
  Clock clock_1 (.out(clock_1_out));
  Hex_Digit_Display hex_digit_display_2 (.value(shifter_1_out));  // open: dp
  Shifter #(.width(4), .shift("lr")) shifter_1 (.in(register_1_q), .\dist (2'b01), .out(shifter_1_out));
  Shifter #(.width(4)) shifter_2 (.in(register_1_q), .\dist (2'b01), .out(shifter_2_out));
  Multiplexer #(.width(4), .enable("false")) multiplexer_1 (
    .in0(shifter_1_out), .in1(adder_1_out), .out(multiplexer_1_out), .sel(register_1_q[0]));
  Adder #(.width(4)) adder_1 (.a(shifter_2_out), .b(register_1_q), .out(adder_1_out), .cin(1'b1));  // open: cout
  Hex_Digit_Display hex_digit_display_3 (.value(adder_1_out));  // open: dp
  Hex_Digit_Display hex_digit_display_4 (.value(multiplexer_1_out));  // open: dp
endmodule
