// Logisim project verrou.circ as structural Verilog: 2 circuits, main circuit main
module main (
  input  H,
  input  \Donnée ,
  output S
);

  wire and_1_out, and_2_out, nor_1_out, not_1_out;

  not not_1 (not_1_out, \Donnée );
  and and_1 (and_1_out, H, \Donnée );
  and and_2 (and_2_out, H, not_1_out);
  nor nor_1 (nor_1_out, S, and_1_out);
  nor nor_2 (S, and_2_out, nor_1_out);

  // Notes on the sheet:
  //   Le verrou
  //   H=0  ==>> Boucle isolée, valeur conservée
  //   H=1  ==>> Boucle affectée par la Donnée
endmodule

module UAL (
  input  [7:0] Op0,
  input  [7:0] Op1,
  input  [2:0] Fun,
  output [7:0] R,
  output N,
  output Z
);

  wire [7:0] adder_1_out, and_1_out, not_1_out, or_1_out, shifter_1_out, subtractor_1_out, xor_1_out;

  assign not_1_out = ~Op0;  // NOT_Gate not_1, 8 bits wide
  Shifter #(.shift("ar")) shifter_1 (.in(Op0), .\dist (3'b001), .out(shifter_1_out));
  Adder adder_1 (.a(Op0), .b(Op1), .out(adder_1_out), .cin(1'b0));  // open: cout
  Subtractor subtractor_1 (.a(Op0), .b(Op1), .out(subtractor_1_out), .bin(1'b0));  // open: bout
  assign and_1_out = Op0 & Op1;  // AND_Gate and_1, 8 bits wide
  assign or_1_out = Op0 | Op1;  // OR_Gate or_1, 8 bits wide
  assign xor_1_out = Op0 ^ Op1;  // XOR_Gate xor_1, 8 bits wide
  Multiplexer #(.select(3), .width(8), .enable("false")) multiplexer_1 (
    .in0(Op0), .in1(not_1_out), .in2(shifter_1_out), .in3(adder_1_out), .in4(subtractor_1_out),
    .in5(and_1_out), .in6(or_1_out), .in7(xor_1_out), .out({N, R[6:0]}), .sel(Fun));
  nor nor_1 (Z, N, R[6], R[5], R[4], R[3], R[2], R[1], R[0]);

  assign R[7] = N;
endmodule
